# Fritzing sketch bot travelling schematics (saved by Fritzing 0.7.5b)
breadboards: 1

parts:
  Arduino1 = Arduino
  LCD1 = LCD screen
  R1 = Rotary Potentiometer (Small) [maximum_resistance=10kΩ]
  S1 = Pushbutton [package="[THT]"]
  S2 = Pushbutton [package="[THT]"]
  S3 = Pushbutton [package="[THT]"]
  S4 = Pushbutton [package="[THT]"]
  R5 = Resistor [tolerance=±5% resistance=10k package=THT]

nets:
  GND: Arduino1.GND, LCD1.VSS, LCD1.R/W, LCD1.LED-, R1.leg2, R5.Pin_1
  N1: Arduino1.D9, LCD1.RS
  N2: Arduino1.D8, LCD1.E
  N3: Arduino1.D7, LCD1.DB4
  N4: Arduino1.D6, LCD1.DB5
  N5: Arduino1.D5, LCD1.DB6
  N6: Arduino1.D4, LCD1.DB7
  +5V: Arduino1.D3, Arduino1.D2, Arduino1.D1TX, Arduino1.D0RX, Arduino1.+5V, LCD1.VDD, LCD1.LED+, R1.leg1, S1.Pin_1, S1.Pin_2, S1.Pin_3, S1.Pin_4, S2.Pin_1, S2.Pin_2, S2.Pin_3, S2.Pin_4, S3.Pin_1, S3.Pin_2, S3.Pin_3, S3.Pin_4, S4.Pin_1, S4.Pin_2, S4.Pin_3, S4.Pin_4, R5.Pin_0
  N7: LCD1.V0, R1.wiper
